# Fritzing sketch esquema (saved by Fritzing 0.9.3b)

parts:
  OLED1 = OLED Mono 0.56 inch blue or white
  Componente1 = Arduino Pro Mini 328 - 3.3 V/8MHz
  U7 = RF-LINK_TX [package=rf-link_tx]
  U8 = RF-LINK_RX [package=rf-link_rx]
  S1 = Pushbutton [package="[THT]"]
  S2 = Pushbutton [package="[THT]"]
  VCC1 = Battery block 9V
  U9 = Mini-360 DC-DC Buck converter [package=THT]
  S3 = Toggle Switch [package=THT]

nets:
  N1: OLED1.SDA, Componente1.A2
  N2: OLED1.SCL, Componente1.A3
  VCC: OLED1.VCC, Componente1.VCC, U9.OUT+
  GND: OLED1.GND, Componente1.GND, U7.GND, U8.GND, S1.Pin_3, S1.Pin_4, S2.Pin_3, S2.Pin_4, U9.OUT-
  N3: Componente1.D10_PWM/SS, U7.DATA
  N4: Componente1.D9_PWM, S2.Pin_1, S2.Pin_2
  N5: Componente1.D8, S1.Pin_1, S1.Pin_2
  N6: Componente1.D2, U8.Data
  +5V: U7.+5V, U8.VCC, U9.IN+, S3.L2
  N7: VCC1.-, U9.IN-
  N8: VCC1.+, S3.COM

notes:
  receptor
  emisor
  5V
  max 12v

custom parts:
  OLED Mono 0.56 inch blue or white: OLED, I2C 3.3V - 5V Blue and White text versions
  Arduino Pro Mini 328 - 3.3 V/8MHz: Versión de Arduino Pro Mini basada en MEGA328P a 8MHz y alimentada a 3.3 voltios.
  RF-LINK_TX: Common RF transmitter of the 315.00Mhz varity
  RF-LINK_RX: RF Link receivers- WRL-8947, 8948, 8949, 8950
  Mini-360 DC-DC Buck converter: Mini-360 DC-DC Buck converter. Tiny buck step down voltage converter, input voltage 4.75 to 23V output 1 to 17V adjustable. Available from ebay and the like.
